// Logisim project control-logic.circ as structural Verilog: 1 circuit, main circuit control_logic
module control_logic (
  input  [31:0] Instruction,
  input  BrEq,
  input  BrLt,
  output PCSel,
  output RegWEn,
  output [2:0] ImmSel,
  output BrUn,
  output ASel,
  output BSel,
  output [3:0] ALUSel,
  output MemWEn,
  output [1:0] WBSel
);

  wire IsAddi, IsAndi, IsOri, IsSlli, IsSlti, IsSrai, IsSrli, IsXori, IType;
  wire [5:0] ITypeInstruction, multiplexer_1_out, RomInput;
  wire [15:14] rom_1_data;

  ROM #(.addrWidth(6), .dataWidth(16)) rom_1 (
    .addr(RomInput), .data({rom_1_data, WBSel, MemWEn, ALUSel, BSel, ASel, BrUn, ImmSel, RegWEn}));
  Comparator #(.width(7)) comparator_1 (.a(Instruction[6:0]), .b(7'b0010011), .eq(IType));  // open: gt, lt
  Multiplexer #(.enable("true"), .width(6)) multiplexer_1 (
    .in0(6'b010011), .in1(6'b010100), .out(multiplexer_1_out), .sel(Instruction[30]), .en(IType));
  Multiplexer #(.enable("true"), .select(3), .width(6)) multiplexer_2 (
    .in0(6'b001111), .in1(6'b010000), .in2(6'b010001), .in3({6{1'b0}}), .in4(6'b010010),
    .in5(multiplexer_1_out), .in6(6'b010101), .in7(6'b010110), .out(ITypeInstruction),
    .sel(Instruction[14:12]), .en(IType));
  Priority_Encoder #(.select_enc(6)) priority_encoder_1 (
    .in15(IsAddi), .in16(IsSlli), .in17(IsSlti), .in18(IsXori), .in19(IsSrli), .in20(IsSrai), .in21(IsOri),
    .in22(IsAndi), .out(RomInput));  // open: in0, in1, in2, in3, in4, in5, in6, in7, in8, in9, in10, in11, in12, in13, in14, in23, in24, in25, in26, in27, in28, in29, in30, in31, in32, in33, in34, in35, in36, in37, in38, in39, in40, in41, in42, in43, in44, in45, in46, in47, in48, in49, in50, in51, in52, in53, in54, in55, in56, in57, in58, in59, in60, in61, in62, in63, gs, en_out, en_in
  Comparator #(.width(6)) comparator_2 (.a(ITypeInstruction), .b(6'b001111), .eq(IsAddi));  // open: gt, lt
  Comparator #(.width(6)) comparator_3 (.a(ITypeInstruction), .b(6'b010000), .eq(IsSlli));  // open: gt, lt
  Comparator #(.width(6)) comparator_4 (.a(ITypeInstruction), .b(6'b010001), .eq(IsSlti));  // open: gt, lt
  Comparator #(.width(6)) comparator_5 (.a(ITypeInstruction), .b(6'b010010), .eq(IsXori));  // open: gt, lt
  Comparator #(.width(6)) comparator_6 (.a(ITypeInstruction), .b(6'b010011), .eq(IsSrli));  // open: gt, lt
  Comparator #(.width(6)) comparator_7 (.a(ITypeInstruction), .b(6'b010100), .eq(IsSrai));  // open: gt, lt
  Comparator #(.width(6)) comparator_8 (.a(ITypeInstruction), .b(6'b010101), .eq(IsOri));  // open: gt, lt
  Comparator #(.width(6)) comparator_9 (.a(ITypeInstruction), .b(6'b010110), .eq(IsAndi));  // open: gt, lt

  assign PCSel = 1'b0;

  // Other names for the same wires on the sheet: ITypeFun3[2:0] = Instruction[14:12];
  //   ITypeFun7[6:0] = Instruction[31:25]

  // Notes on the sheet:
  //   INPUTS to your circuit
  //   Connect ROM Input here ->
  //   contents of rom_1 (hex, n*v repeats v):
  //   15*0 1041 10d1 1141 1251 12d1 16c1 1351 13d1
  //   ROM FOR CONTROL LOGIC
  //   DON'T CHANGE THE LOCATIONS OF THE INPUTS AND OUTPUTS!
  //   This is only if you choose to do the ROM option
  //   CONNECT
  //   WIRE
  //   TO
  //   USE
  //   ROM
  //   OUTPUT from your circuit
  //   Reminder: If using ROM, use combinational logic for PCSel
endmodule
